# Fritzing sketch Circuit Schematic (saved by Fritzing 0.9.1b)
breadboards: 1

parts:
  Part1 = Arduino Uno (Rev3)
  U1 = 74HC595 [package="DIP16 [THT]"]
  U2 = 74HC595 [package="DIP16 [THT]"]
  U3 = 74HC595 [package="DIP16 [THT]"]
  U4 = 74HC595 [package="DIP16 [THT]"]
  U5 = 74HC595 [package="DIP16 [THT]"]
  U6 = 74HC595 [package="DIP16 [THT]"]
  U7 = 74HC595 [package="DIP16 [THT]"]
  U8 = 74HC595 [package="DIP16 [THT]"]
  U9 = 74HC595 [package="DIP16 [THT]"]
  U10 = 74HC595 [package="DIP16 [THT]"]
  U11 = 74HC595 [package="DIP16 [THT]"]

nets:
  N1: Part1.D8, U1.ST_CP, U2.ST_CP, U3.ST_CP, U4.ST_CP, U5.ST_CP, U6.ST_CP, U7.ST_CP, U8.ST_CP, U9.ST_CP, U10.ST_CP, U11.ST_CP
  N2: Part1.D10_PWM/SS, U1.SH_CP, U2.SH_CP, U3.SH_CP, U4.SH_CP, U5.SH_CP, U6.SH_CP, U7.SH_CP, U8.SH_CP, U9.SH_CP, U10.SH_CP, U11.SH_CP
  GND: Part1.GND, U1.GND, U1.OE, U2.GND, U2.OE, U3.GND, U4.GND, U4.OE, U5.GND, U5.OE, U6.GND, U6.OE, U7.GND, U7.OE, U8.GND, U8.OE, U9.GND, U9.OE, U10.GND, U10.OE, U11.GND, U11.OE
  N3: Part1.D6_PWM, U8.DS
  VCC: Part1.5V, U1.MR, U1.VCC, U2.MR, U2.VCC, U3.MR, U3.VCC, U4.MR, U4.VCC, U5.MR, U5.VCC, U6.MR, U6.VCC, U7.MR, U7.VCC, U8.MR, U8.VCC, U9.MR, U9.VCC, U10.MR, U10.VCC, U11.MR, U11.VCC
  5V: Part1.VIN
  GND_2: Part1.N/C
  N4: U1.Q7', U5.DS
  N5: U1.DS, U2.Q7'
  N6: U2.DS, U7.Q7'
  N7: U3.Q7', U7.DS
  N8: U3.DS, U6.Q7'
  N9: U4.DS, U5.Q7'
  N10: U6.DS, U11.Q7'
  N11: U8.Q7', U9.DS
  N12: U9.Q7', U10.DS
  N13: U10.Q7', U11.DS
